# Fritzing sketch arduino_isp_harness (saved by Fritzing 1.0.8)

parts:
  isp_probe = IR ISP probe
  isp_anvil = IR ground anvil
  isp_target = Ring IR target
  isp_supply = Selected target VCC
  UNO_-_ArduinoISP = Arduino Uno (Rev3)

nets:
  N1: isp_probe.J1.1_MISO, isp_probe.P2_MISO, isp_target.TP2_PB1, UNO_-_ArduinoISP.D12/MISO
  N2: isp_probe.J1.2_VCC, isp_probe.P9_VCC, isp_target.TP9_VCC, isp_supply.Selected_target_VCC
  N3: isp_probe.J1.3_SCK, isp_probe.P3_SCK, isp_target.TP3_PB2, UNO_-_ArduinoISP.D13/SCK
  N4: isp_probe.J1.4_MOSI, isp_probe.P1_MOSI, isp_target.TP1_PB0, UNO_-_ArduinoISP.D11_PWM/MOSI
  N5: isp_probe.J1.5_RESET, isp_probe.P6_RESET, isp_target.TP6_PB5, UNO_-_ArduinoISP.D10_PWM/SS
  N6: isp_probe.J1.6_GND, isp_probe.J2_GND, isp_anvil.Anvil_J1_GND, isp_anvil.P8_/_P8L_/_P8R_GND, isp_target.TP8_GND, isp_supply.Common_GND, UNO_-_ArduinoISP.GND

notes:
  Arduino Uno ArduinoISP -> programming clip -> Ring IR PCBGREEN MISO | RED VCC | BLUE SCK | YELLOW MOSI | ORANGE RESET | BLACK GND
  J1 = board-top view. Right-hand links represent spring/flat contacts, NOT extra cables.
  HOST: Arduino Uno / ATmega328P
  Load File > Examples > 11.ArduinoISP > ArduinoISP.
  D12=MISO, D11=MOSI, D13=SCK, D10=target RESET.
  Do NOT use Uno RESET or the USB-interface ICSP header.
  POWER / SAFETY - READ BEFORE CONNECTING
  REMOVE CR2032. Wire and check continuity with all power OFF.
  Select ONE compatible target VCC. Uno 5V and 3V3 are intentionally NOT wired.
  Uno I/O is 5V: direct signal wires require a target qualified for that level.
  For lower-voltage targets use a compatible ISP host or verified SPI level translation (not shown).
  Uno 3V3 power does NOT change its I/O levels. Do not join supply outputs.
  Diagram colours are a proposed convention, not a reading of the photo's wire colours.
  BLACK inter-jaw lead is essential.
  J1.6 -> probe J2 -> insulated slack wire -> anvil J1 -> P8 / P8L+P8R -> front TP8.
  Fence and lower guide are mechanical; do not populate their header.

custom parts:
  IR ISP probe: ISP harness interface only; not a PCB layout or approved voltage converter. Artwork: Lantern Ring contributors, CC BY-SA 3.0. Created with Fritzing.
  IR ground anvil: ISP harness interface only; not a PCB layout or approved voltage converter. Artwork: Lantern Ring contributors, CC BY-SA 3.0. Created with Fritzing.
  Ring IR target: ISP harness interface only; not a PCB layout or approved voltage converter. Artwork: Lantern Ring contributors, CC BY-SA 3.0. Created with Fritzing.
  Selected target VCC: ISP harness interface only; not a PCB layout or approved voltage converter. Artwork: Lantern Ring contributors, CC BY-SA 3.0. Created with Fritzing.
